// Logisim project test.circ as structural Verilog: 3 circuits, main circuit frontend
module backend (
  input  in_1,
  input  in_2,
  input  [6:0] keyboard_data,
  output [6:0] terminal_data,
  output terminal_active,
  output keyboard_active
);

  wire cdm16_1_p1, cdm16_1_p3, cdm16_1_p4, cdm16_1_p5, Clock, comparator_1_eq, comparator_2_gt,
       comparator_3_eq, comparator_4_eq, comparator_5_eq, handsmemMux, mem, memMux, not_2_out, RAM, rd, ROM,
       word;
  wire [1:0] not_1_out;
  wire [15:0] addr, cdm16_1_p11, controlled_buffer_2_out, data, handsMemIn, kbdMemIn, multiplexer_2_out;
  wire [15:7] cdm16_1_p10;

  assign not_1_out = ~{in_1, in_2};  // NOT_Gate not_1, 2 bits wide
  Comparator #(.width(16)) comparator_1 (.a(addr), .b(16'hf00d), .eq(comparator_1_eq));  // open: gt, lt
  assign handsMemIn = {{14{1'b0}}, not_1_out};  // Bit_Extender bit_extender_1
  Clock clock_1 (.out(Clock));
  and and_1 (handsmemMux, rd, mem, ~word, comparator_1_eq);  // AND_Gate
  Comparator #(.width(16), .mode("unsigned")) comparator_2 (
    .a(addr), .b(16'hdead), .gt(comparator_2_gt));  // open: eq, lt
  // Probe on cdm16_1_p4
  // Probe on cdm16_1_p1
  // Probe on cdm16_1_p3
  // cdm16 cdm16_1: pin names not known; wires that end beside it: cdm16_1_p1, Clock, cdm16_1_p3, cdm16_1_p4, cdm16_1_p5, mem, rd, word, addr, {cdm16_1_p10, terminal_data}, cdm16_1_p11
  // Probe on cdm16_1_p5
  Multiplexer #(.width(16), .enable("false")) multiplexer_1 (
    .in0(multiplexer_2_out), .in1(handsMemIn), .out(cdm16_1_p11), .sel(handsmemMux));
  Comparator #(.width(16)) comparator_3 (.a(addr), .b(16'hbeef), .eq(comparator_3_eq));  // open: gt, lt
  Comparator #(.width(16)) comparator_4 (.a(addr), .b(16'hbeef), .eq(comparator_4_eq));  // open: gt, lt
  and and_2 (ROM, mem, ~comparator_2_gt);  // AND_Gate
  and and_3 (RAM, mem, comparator_2_gt);
  Multiplexer #(.width(16), .enable("false")) multiplexer_2 (
    .in0(controlled_buffer_2_out), .in1(kbdMemIn), .out(multiplexer_2_out), .sel(memMux));
  Comparator #(.width(16)) comparator_5 (.a(addr), .b(16'hdead), .eq(comparator_5_eq));  // open: gt, lt
  and and_4 (memMux, rd, mem, ~word, comparator_3_eq);  // AND_Gate
  and and_5 (keyboard_active, ~rd, mem, ~word, comparator_4_eq);  // AND_Gate
  and and_6 (terminal_active, ~rd, mem, ~word, comparator_5_eq);  // AND_Gate
  // RAM ram_1: pin names not known; wires that end beside it: addr, word, RAM, Clock, rd, data
  // ROM rom_1: pin names not known; wires that end beside it: addr, ROM, word, data
  not not_2 (not_2_out, rd);
  assign data = not_2_out ? {cdm16_1_p10, terminal_data} : 16'bz;  // Controlled_Buffer controlled_buffer_1
  assign controlled_buffer_2_out = rd ? data : 16'bz;  // Controlled_Buffer controlled_buffer_2
  assign kbdMemIn = {{9{1'b0}}, keyboard_data};  // Bit_Extender bit_extender_2
endmodule

module frontend (
);

  wire backend_1_keyboard_active, backend_1_terminal_active, pull_resistor_1_node, pull_resistor_2_node;
  wire [6:0] backend_1_terminal_data, keyboard_1_data;

  Pull_Resistor pull_resistor_1 (.node(pull_resistor_1_node));
  TTY tty_1 (.data(backend_1_terminal_data), .clk(backend_1_terminal_active));  // open: we, clr
  Keyboard keyboard_1 (.clk(backend_1_keyboard_active), .data(keyboard_1_data));  // open: re, clr, avail
  backend backend_1 (
    .terminal_data(backend_1_terminal_data), .terminal_active(backend_1_terminal_active),
    .in_1(pull_resistor_2_node), .in_2(pull_resistor_1_node), .keyboard_data(keyboard_1_data),
    .keyboard_active(backend_1_keyboard_active));
  Pull_Resistor pull_resistor_2 (.node(pull_resistor_2_node));
endmodule

module hint (
);


  // Notes on the sheet:
  //   strings
endmodule
