// Logisim project test.circ as structural Verilog: 2 circuits, main circuit main
module main (
);

  wire button_1_out, button_2_out, button_3_out, clock_1_out;
  wire [7:0] inner_circuit_1_res;

  Button button_1 (.out(button_1_out));
  Button button_2 (.out(button_2_out));
  Button button_3 (.out(button_3_out));
  Clock clock_1 (.out(clock_1_out));
  inner_circuit inner_circuit_1 (
    .plus_1(button_1_out), .plus_10(button_2_out), .reset(button_3_out), .clk(clock_1_out),
    .res(inner_circuit_1_res));
  Hex_Digit_Display hex_digit_display_1 (.value(inner_circuit_1_res[7:4]));  // open: dp
  Hex_Digit_Display hex_digit_display_2 (.value(inner_circuit_1_res[3:0]));  // open: dp
endmodule

module inner_circuit (
  input  plus_1,
  input  plus_10,
  input  reset,
  input  clk,
  output [7:0] res
);

  wire [7:0] adder_1_out, adder_2_out, multiplexer_1_out, multiplexer_2_out, multiplexer_3_out;

  Adder adder_1 (.a(res), .b(8'h1), .out(adder_1_out));  // open: cin, cout
  Adder adder_2 (.a(res), .b(8'ha), .out(adder_2_out));  // open: cin, cout
  Multiplexer #(.width(8), .enable("false")) multiplexer_1 (
    .in0(res), .in1(adder_1_out), .out(multiplexer_1_out), .sel(plus_1));
  Multiplexer #(.width(8), .enable("false")) multiplexer_2 (
    .in0(multiplexer_1_out), .in1(adder_2_out), .out(multiplexer_2_out), .sel(plus_10));
  Multiplexer #(.width(8), .enable("false")) multiplexer_3 (
    .in0(multiplexer_2_out), .in1({8{1'b0}}), .out(multiplexer_3_out), .sel(reset));
  Register register_1 (.D(multiplexer_3_out), .en(1'b1), .Q(res), .clk(clk));  // open: clr

  // Other names for the same wires on the sheet: reg_out[7:0] = res
endmodule
