// Logisim project test2.circ as structural Verilog: 1 circuit, main circuit main
module main (
  input  [2:0] in_1
);

  wire and_1_out, and_2_out, and_3_out, button_1_out, cdm_8_mark5_1_p3, cdm_8_mark5_1_p4, cdm_8_mark5_1_p5,
       cdm_8_mark5_1_p7, cdm_8_mark5_1_p8, cdm_8_mark5_1_p9, cdm_8_mark5_1_p10, cdm_8_mark5_1_p11,
       cdm_8_mark5_1_p12, cdm_8_mark5_1_p13, cdm_8_mark5_1_p14, clk, decoder_1_out0, decoder_1_out1,
       not_1_out, or_1_out, zero_periph;
  wire [0:0] button_2_out;
  wire [6:0] bit_extender_1_out, keyboard_1_data;
  wire [7:0] bit_extender_2_out, cdm_8_mark5_1_p16, cdm_8_mark5_1_p17, controlled_buffer_1_out;
  wire [15:0] cdm_8_mark5_1_p15;

  Button button_1 (.out(button_1_out));
  Button button_2 (.out(button_2_out[0]));
  Clock clock_1 (.out(clk));
  or or_1 (or_1_out, button_1_out, button_2_out[0]);
  LED led_1 (.in(cdm_8_mark5_1_p3));
  // Probe on cdm_8_mark5_1_p4
  // Probe on cdm_8_mark5_1_p5
  // Probe on cdm_8_mark5_1_p7
  // Probe on cdm_8_mark5_1_p11
  // Probe on cdm_8_mark5_1_p9
  // Probe on cdm_8_mark5_1_p8
  // Probe on cdm_8_mark5_1_p10
  Decoder #(.disabled(0)) decoder_1 (
    .out0(decoder_1_out0), .out1(decoder_1_out1), .sel(cdm_8_mark5_1_p12), .en(cdm_8_mark5_1_p13));
  // CdM_8_mark5 cdm_8_mark5_1: pin names not known; wires that end beside it: or_1_out, {2'b00, button_2_out[0]}, cdm_8_mark5_1_p3, cdm_8_mark5_1_p4, cdm_8_mark5_1_p5, clk, cdm_8_mark5_1_p7, cdm_8_mark5_1_p8, cdm_8_mark5_1_p9, cdm_8_mark5_1_p10, cdm_8_mark5_1_p11, cdm_8_mark5_1_p12, cdm_8_mark5_1_p13, cdm_8_mark5_1_p14, cdm_8_mark5_1_p15, cdm_8_mark5_1_p16, cdm_8_mark5_1_p17
  not not_1 (not_1_out, cdm_8_mark5_1_p14);
  assign controlled_buffer_1_out = not_1_out ? cdm_8_mark5_1_p16 : 8'bz;  // Controlled_Buffer controlled_buffer_1
  assign cdm_8_mark5_1_p17 = cdm_8_mark5_1_p14 ? controlled_buffer_1_out : 8'bz;  // Controlled_Buffer controlled_buffer_2
  and and_1 (and_1_out, ~zero_periph, decoder_1_out1);  // AND_Gate
  // Probe on controlled_buffer_1_out
  Bit_Extender #(.out_width(7), .\type ("sign")) bit_extender_1 (
    .in(controlled_buffer_1_out), .out(bit_extender_1_out));
  TTY tty_1 (.data(bit_extender_1_out), .clk(clk), .we(and_2_out));  // open: clr
  and and_2 (and_2_out, decoder_1_out1, ~cdm_8_mark5_1_p14, zero_periph);  // AND_Gate
  and and_3 (and_3_out, decoder_1_out1, cdm_8_mark5_1_p14, zero_periph);
  Comparator #(.width(16)) comparator_1 (.a(cdm_8_mark5_1_p15), .b({16{1'b0}}), .eq(zero_periph));  // open: gt, lt
  // RAM ram_1: pin names not known; wires that end beside it: cdm_8_mark5_1_p15[7:0], and_1_out, clk, cdm_8_mark5_1_p14, controlled_buffer_1_out
  // ROM rom_1: pin names not known; wires that end beside it: cdm_8_mark5_1_p15, decoder_1_out0, 1'b1, controlled_buffer_1_out
  Keyboard #(.trigger("falling")) keyboard_1 (.clk(clk), .re(and_3_out), .data(keyboard_1_data));  // open: clr, avail
  assign controlled_buffer_1_out = and_3_out ? bit_extender_2_out : 8'bz;  // Controlled_Buffer controlled_buffer_3
  assign bit_extender_2_out = {{1{1'b0}}, keyboard_1_data};  // Bit_Extender bit_extender_2

  // Notes on the sheet:
  //   RAM
  //   ROM
endmodule
